// Logisim project single_cycle_datatpath.circ as structural Verilog: 8 circuits, main circuit single_cycle_datapath
module single_cycle_datapath (
  output [6:0] out_1
);

  wire ALU_branch, and_1_out, clock_1_out, Control_alusrc, Control_branch, Control_memread, Control_memtoreg,
       Control_memwrite, Control_regwrite, Control_slt;
  wire [1:0] Control_aluop;
  wire [31:0] adder_1_out, adder_2_out, ALU_aluresult, Immediate_output, Memory_data_2, multiplexer_1_out,
       multiplexer_2_out, multiplexer_3_out, multiplexer_4_out, Program_Counter_output, Registers_data1,
       Registers_data2, shifter_1_out, shifter_2_out;
  wire [31:7] Instruction_Memory_instruction;

  Clock clock_1 (.out(clock_1_out));
  program_counter Program_Counter (
    .Input(multiplexer_2_out), .Branch(and_1_out), .Clock(clock_1_out), .Output(Program_Counter_output));
  instruction_memory Instruction_Memory (
    .InstructionNumber(Program_Counter_output), .Clock(clock_1_out),
    .Instruction({Instruction_Memory_instruction, out_1}));
  Adder #(.width(32)) adder_1 (.a(Program_Counter_output), .b(32'h1), .out(adder_1_out));  // open: cin, cout
  control Control (
    .Opcode(out_1), .funct3(Instruction_Memory_instruction[14:12]),
    .func7(Instruction_Memory_instruction[31:25]), .slt(Control_slt), .Branch(Control_branch),
    .MemToReg(Control_memtoreg), .ALUOp(Control_aluop), .MemWrite(Control_memwrite), .ALUSrc(Control_alusrc),
    .RegWrite(Control_regwrite), .MemRead(Control_memread));
  ImmGen Immediate (
    .Opcode(out_1), .Input({Instruction_Memory_instruction, out_1}), .Output(Immediate_output));  // open: out_4
  registers Registers (
    .RegWrite(Control_regwrite), .DataW(multiplexer_4_out), .Rd(Instruction_Memory_instruction[11:7]),
    .Clock(clock_1_out), .Rs1(Instruction_Memory_instruction[19:15]),
    .Rs2(Instruction_Memory_instruction[24:20]), .Data1(Registers_data1), .Data2(Registers_data2));
  Multiplexer #(.width(32)) multiplexer_1 (
    .in0(Registers_data2), .in1(Immediate_output), .out(multiplexer_1_out), .sel(Control_alusrc));  // open: en
  Shifter #(.width(32), .shift("lr")) shifter_1 (.in(Immediate_output), .\dist (5'b00001), .out(shifter_1_out));
  Adder #(.width(32)) adder_2 (.a(Program_Counter_output), .b(shifter_1_out), .out(adder_2_out));  // open: cin, cout
  ALU ALU (
    .Data1(Registers_data1), .Data2(multiplexer_1_out), .Branch(ALU_branch), .ALUop(Control_aluop),
    .slt(Control_slt), .ALUresult(ALU_aluresult));
  Multiplexer #(.width(32)) multiplexer_2 (
    .in0(adder_1_out), .in1(adder_2_out), .out(multiplexer_2_out), .sel(and_1_out));  // open: en
  and and_1 (and_1_out, Control_branch, ALU_branch);
  data_memory Memory (
    .Address(ALU_aluresult), .Data(Registers_data2), .Clock(clock_1_out), .MemWrite(Control_memwrite),
    .MemRead(Control_memread), .Data_2(Memory_data_2));
  Shifter #(.width(32)) shifter_2 (.in(adder_1_out), .\dist (5'b00010), .out(shifter_2_out));
  Multiplexer #(.width(32)) multiplexer_3 (
    .in0(Memory_data_2), .in1(ALU_aluresult), .out(multiplexer_3_out), .sel(Control_memtoreg));  // open: en
  Multiplexer #(.width(32)) multiplexer_4 (
    .in0(multiplexer_3_out), .in1(shifter_2_out), .out(multiplexer_4_out), .sel(and_1_out));  // open: en

  // Notes on the sheet:
  //   rs1
  //   rs2
  //   rd
  //   Curent state is not working, it does write five to the register though
endmodule

module program_counter (
  input  Branch,
  input  [31:0] Input,
  input  Clock,
  output [31:0] Output
);

  wire not_1_out;

  not not_1 (not_1_out, Branch);
  Counter #(.width(32), .max('hffffffff)) counter_1 (
    .load(Branch), .D(Input), .count(not_1_out), .Q(Output), .clk(Clock));  // open: carry, clr

  // Notes on the sheet:
  //   Seems to be working
endmodule

module instruction_memory (
  input  [31:0] InstructionNumber,
  input  Clock,
  output [31:0] Instruction
);

  wire [15:0] bit_extender_1_out;

  Bit_Extender #(.in_width(32)) bit_extender_1 (.in(InstructionNumber), .out(bit_extender_1_out));
  RAM #(.addrWidth(16), .dataWidth(32)) ram_1 (
    .addr(bit_extender_1_out), .data(Instruction), .clk(Clock), .ld(1'b1));  // open: sel, clr

  // Notes on the sheet:
  //   Seems to be working
endmodule

module registers (
  input  RegWrite,
  input  [31:0] DataW,
  input  [4:0] Rd,
  input  Clock,
  input  [4:0] Rs1,
  input  [4:0] Rs2,
  output [31:0] Data1,
  output [31:0] Data2
);

  wire demultiplexer_1_out0, demultiplexer_1_out1, demultiplexer_1_out2, demultiplexer_1_out3,
       demultiplexer_1_out4, demultiplexer_1_out5, demultiplexer_1_out6, demultiplexer_1_out7,
       demultiplexer_1_out8, demultiplexer_1_out9;
  wire [31:0] register_1_q, register_2_q, register_3_q, register_4_q, register_5_q, register_6_q,
       register_7_q, register_8_q, register_9_q, register_10_q;

  Demultiplexer #(.select(5)) demultiplexer_1 (
    .out0(demultiplexer_1_out0), .out1(demultiplexer_1_out1), .out2(demultiplexer_1_out2),
    .out3(demultiplexer_1_out3), .out4(demultiplexer_1_out4), .out5(demultiplexer_1_out5),
    .out6(demultiplexer_1_out6), .out7(demultiplexer_1_out7), .out8(demultiplexer_1_out8),
    .out9(demultiplexer_1_out9), .in(RegWrite), .sel(Rd));  // open: out10, out11, out12, out13, out14, out15, out16, out17, out18, out19, out20, out21, out22, out23, out24, out25, out26, out27, out28, out29, out30, out31, en
  Register #(.width(32)) register_1 (.D(DataW), .en(demultiplexer_1_out0), .Q(register_1_q), .clk(Clock));  // open: clr
  Register #(.width(32)) register_2 (.D(DataW), .en(demultiplexer_1_out1), .Q(register_2_q), .clk(Clock));  // open: clr
  Register #(.width(32)) register_3 (.D(DataW), .en(demultiplexer_1_out2), .Q(register_3_q), .clk(Clock));  // open: clr
  Register #(.width(32)) register_4 (.D(DataW), .en(demultiplexer_1_out3), .Q(register_4_q), .clk(Clock));  // open: clr
  Register #(.width(32)) register_5 (.D(DataW), .en(demultiplexer_1_out4), .Q(register_5_q), .clk(Clock));  // open: clr
  Register #(.width(32)) register_6 (.D(DataW), .en(demultiplexer_1_out5), .Q(register_6_q), .clk(Clock));  // open: clr
  Register #(.width(32)) register_7 (.D(DataW), .en(demultiplexer_1_out6), .Q(register_7_q), .clk(Clock));  // open: clr
  Register #(.width(32)) register_8 (.D(DataW), .en(demultiplexer_1_out7), .Q(register_8_q), .clk(Clock));  // open: clr
  Register #(.width(32)) register_9 (.D(DataW), .en(demultiplexer_1_out8), .Q(register_9_q), .clk(Clock));  // open: clr
  Register #(.width(32)) register_10 (
    .D(DataW), .en(demultiplexer_1_out9), .Q(register_10_q), .clk(Clock));  // open: clr
  Multiplexer #(.select(5), .width(32)) multiplexer_1 (
    .in0(register_1_q), .in1(register_2_q), .in2(register_3_q), .in3(register_4_q), .in4(register_5_q),
    .in5(register_6_q), .in6(register_7_q), .in7(register_8_q), .in8(register_9_q), .in9(register_10_q),
    .out(Data1), .sel(Rs1));  // open: in10, in11, in12, in13, in14, in15, in16, in17, in18, in19, in20, in21, in22, in23, in24, in25, in26, in27, in28, in29, in30, in31, en
  Multiplexer #(.select(5), .width(32)) multiplexer_2 (
    .in0(register_1_q), .in1(register_2_q), .in2(register_3_q), .in3(register_4_q), .in4(register_5_q),
    .in5(register_6_q), .in6(register_7_q), .in7(register_8_q), .in8(register_9_q), .in9(register_10_q),
    .out(Data2), .sel(Rs2));  // open: in10, in11, in12, in13, in14, in15, in16, in17, in18, in19, in20, in21, in22, in23, in24, in25, in26, in27, in28, in29, in30, in31, en

  // Notes on the sheet:
  //   Seems to be working, needs testing
endmodule

module ALU (
  input  [31:0] Data1,
  input  [31:0] Data2,
  input  [1:0] ALUop,
  input  slt,
  output Branch,
  output [31:0] ALUresult
);

  wire comparator_1_lt;
  wire [31:0] adder_1_out, and_1_out, bit_extender_1_out, multiplexer_1_out, or_1_out, subtractor_1_out;

  Adder #(.width(32)) adder_1 (.a(Data1), .b(Data2), .out(adder_1_out));  // open: cin, cout
  Subtractor #(.width(32)) subtractor_1 (.a(Data1), .b(Data2), .out(subtractor_1_out));  // open: bin, bout
  assign and_1_out = Data1 & Data2;  // AND_Gate and_1, 32 bits wide
  assign or_1_out = Data1 | Data2;  // OR_Gate or_1, 32 bits wide
  Comparator #(.width(32)) comparator_1 (.a(Data1), .b(Data2), .eq(Branch), .lt(comparator_1_lt));  // open: gt
  Multiplexer #(.select(2), .width(32)) multiplexer_1 (
    .in0(adder_1_out), .in1(subtractor_1_out), .in2(and_1_out), .in3(or_1_out), .out(multiplexer_1_out),
    .sel(ALUop));  // open: en
  assign bit_extender_1_out = {{31{1'b0}}, comparator_1_lt};  // Bit_Extender bit_extender_1
  Multiplexer #(.width(32)) multiplexer_2 (
    .in0(multiplexer_1_out), .in1(bit_extender_1_out), .out(ALUresult), .sel(slt));  // open: en

  // Notes on the sheet:
  //   No idea if works properly, needs a lot of testing
endmodule

module data_memory (
  input  [31:0] Address,
  input  [31:0] Data,
  input  Clock,
  input  MemWrite,
  input  MemRead,
  output [31:0] Data_2
);

  wire [15:0] bit_extender_1_out;

  Bit_Extender #(.in_width(32)) bit_extender_1 (.in(Address), .out(bit_extender_1_out));
  RAM #(.addrWidth(16), .dataWidth(32), .bus("separate")) ram_1 (
    .addr(bit_extender_1_out), .din(Data), .data(Data_2), .str(MemWrite), .clk(Clock), .ld(MemRead));  // open: sel, clr

  // Notes on the sheet:
  //   No idea if it is working, needs testing
endmodule

module control (
  input  [6:0] Opcode,
  input  [2:0] funct3,
  input  [6:0] func7,
  output Branch,
  output MemToReg,
  output [1:0] ALUOp,
  output MemWrite,
  output ALUSrc,
  output RegWrite,
  output MemRead,
  output slt
);

  wire addi_out, and_1_out, and_2_out, and_3_out, and_4_out, and_5_out, and_6_out, AND_7_out, and_8_out,
       beq_out, jal_out, not_1_out, not_2_out, not_3_out, not_4_out, not_5_out, not_6_out, not_7_out,
       not_8_out, not_9_out, not_10_out, not_11_out, not_12_out, not_13_out, not_14_out, not_15_out,
       not_16_out, not_17_out, not_18_out, not_19_out, not_20_out, or_1_out, or_2_out, OR_3_out, r_type_out;

  not not_1 (not_1_out, addi_out);
  and r_type (r_type_out, Opcode[0], Opcode[1], Opcode[4], Opcode[5]);
  not not_2 (not_2_out, and_1_out);
  and and_1 (and_1_out, not_3_out, and_4_out);
  not not_3 (not_3_out, func7[5]);
  not not_4 (not_4_out, funct3[0]);
  not not_5 (not_5_out, Opcode[5]);
  and addi (addi_out, Opcode[0], not_5_out, Opcode[1], Opcode[4]);
  or or_1 (or_1_out, and_2_out, OR_3_out);
  and and_2 (and_2_out, not_2_out, and_3_out);
  and and_3 (and_3_out, and_5_out, and_6_out);
  and and_4 (and_4_out, not_4_out, not_6_out, not_7_out);
  not not_6 (not_6_out, funct3[1]);
  not not_7 (not_7_out, funct3[2]);
  not not_8 (not_8_out, funct3[0]);
  and and_5 (and_5_out, not_1_out, func7[5]);
  not not_9 (not_9_out, Opcode[3]);
  not not_10 (not_10_out, Opcode[5]);
  not not_11 (not_11_out, Opcode[4]);
  and lw (MemRead, Opcode[1], not_9_out, not_10_out, not_11_out, Opcode[0]);
  and and_6 (and_6_out, not_8_out, not_13_out, not_12_out);
  not not_12 (not_12_out, funct3[2]);
  not not_13 (not_13_out, funct3[1]);
  not not_14 (not_14_out, Opcode[4]);
  not not_15 (not_15_out, Opcode[6]);
  not not_16 (not_16_out, Opcode[3]);
  and sw (MemWrite, Opcode[1], Opcode[0], not_16_out, not_14_out, not_15_out, Opcode[5]);
  or or_2 (or_2_out, AND_7_out, OR_3_out);
  and AND_7 (AND_7_out, funct3[0], funct3[1], funct3[2]);
  and OR_3 (OR_3_out, not_17_out, funct3[1], funct3[2]);
  not not_17 (not_17_out, funct3[0]);
  not not_18 (not_18_out, Opcode[3]);
  and beq (beq_out, Opcode[0], Opcode[1], not_18_out, Opcode[5], Opcode[6]);
  and jal (jal_out, Opcode[0], Opcode[1], Opcode[3], Opcode[2], Opcode[5], Opcode[6]);
  or or_4 (ALUOp[0], beq_out, or_1_out);
  xor xor_1 (ALUOp[1], beq_out, or_2_out);
  not not_19 (not_19_out, funct3[0]);
  not not_20 (not_20_out, funct3[2]);
  and and_8 (and_8_out, not_20_out, funct3[1], not_19_out);
  and and_9 (slt, and_8_out, r_type_out);
  not not_21 (MemToReg, MemRead);
  or or_5 (Branch, jal_out, beq_out);
  or or_6 (ALUSrc, addi_out, MemWrite, MemRead);
  or or_7 (RegWrite, MemRead, jal_out, addi_out, r_type_out);

  // Notes on the sheet:
  //   Seems to be working, needs testing
endmodule

module ImmGen (
  input  [6:0] Opcode,
  input  [31:0] Input,
  output [31:0] Output,
  output [2:0] out_4
);

  wire not_1_out, not_2_out, not_3_out, not_4_out, not_5_out, not_6_out, not_7_out;
  wire [31:0] bit_extender_1_out, bit_extender_2_out, bit_extender_3_out, bit_extender_4_out,
       bit_extender_5_out, bit_extender_6_out;

  not not_1 (not_1_out, Opcode[5]);
  not not_2 (not_2_out, Opcode[4]);
  not not_3 (not_3_out, Opcode[3]);
  // AND_Gate lw has open pins: in0=Opcode[1], in1=not_3_out, in2=not_1_out, in3=not_2_out, in4=Opcode[0], out=open
  not not_4 (not_4_out, Opcode[6]);
  not not_5 (not_5_out, Opcode[4]);
  not not_6 (not_6_out, Opcode[3]);
  and sw (out_4[0], Opcode[1], Opcode[0], not_6_out, not_5_out, not_4_out, Opcode[5]);
  not not_7 (not_7_out, Opcode[3]);
  and beq (out_4[1], Opcode[0], Opcode[1], not_7_out, Opcode[5], Opcode[6]);
  assign bit_extender_1_out = {{12{1'b0}}, Input[31:12]};  // Bit_Extender bit_extender_1
  assign bit_extender_2_out = {{20{1'b0}}, {Input[31], Input[7], Input[30:25], Input[11:8]}};  // Bit_Extender bit_extender_2
  assign bit_extender_3_out = {{20{1'b0}}, {Input[31:25], Input[11:7]}};  // Bit_Extender bit_extender_3
  assign bit_extender_4_out = {{20{Input[31]}}, Input[31:20]};  // Bit_Extender bit_extender_4
  assign bit_extender_5_out = {{20{1'b1}}, Input[31:20]};  // Bit_Extender bit_extender_5
  and jal (out_4[2], Opcode[0], Opcode[1], Opcode[3], Opcode[2], Opcode[5], Opcode[6]);
  assign bit_extender_6_out = {{12{1'b0}}, {Input[31], Input[19:12], Input[20], Input[30:21]}};  // Bit_Extender bit_extender_6
  Multiplexer #(.width(32)) multiplexer_1 (.in1(bit_extender_5_out));  // open: in0, out, sel, en
  Multiplexer #(.select(3), .width(32)) multiplexer_2 (
    .in0(bit_extender_4_out), .in1(bit_extender_3_out), .in2(bit_extender_2_out), .in3(bit_extender_1_out),
    .in4(bit_extender_6_out), .out(Output), .sel(out_4));  // open: in5, in6, in7, en

  // Notes on the sheet:
  //   U
  //   SB
  //   I
  //   UJ
  //   S
  //   Seems to be working, needs implementation of control signal
endmodule
